# Fritzing sketch Ahmad_SolarPanel_Test1 (saved by Fritzing 0.9.3b)
circuit board: 1.90336cm x 5.15143cm
breadboards: 1

parts:
  Part1 = adafruit [part_number="Adafruit #1085"]
  Raspberry_Pi_1 = Raspberry Pi 3 [part_number=RPI-3-V1.2]
  ACS712_Current_Sensor1 = ACS712 Current Sensor

nets:
  N1: Part1.connector13, ACS712_Current_Sensor1.OUT
  N2: Part1.connector16, Raspberry_Pi_1.GPIO3
  N3: Part1.connector17, Raspberry_Pi_1.GPIO2
  GND: Part1.connector18, Raspberry_Pi_1.GND, Raspberry_Pi_1.GPIO18, ACS712_Current_Sensor1.GND
  3V3: Part1.connector19, Raspberry_Pi_1.3v3, ACS712_Current_Sensor1.VCC

custom parts:
  ACS712 Current Sensor: A breakout board for the Allegro ACS712 is a Hall Effect-based linear current sensor. The module operates at 5V.
